# Fritzing sketch text (saved by Fritzing 0.9.3b)
breadboards: 1

parts:
  R1 = Resistor [tolerance=±5% resistance=10k package=THT]
  R2 = Resistor [tolerance=±5% resistance=220 package=THT]
  LCD1 = LCD screen
  Part1 = Arduino Uno (Rev3)

nets:
  N1: R1.Pin_0, LCD1.DB3, LCD1.DB7, LCD1.LED+, Part1.GND
  N2: R1.Pin_1, R2.Pin_1, Part1.5V
  N3: R2.Pin_0, LCD1.LED-
  N4: LCD1.VSS, Part1.A0
  N5: LCD1.VDD, Part1.A1
  N6: LCD1.V0, Part1.A2
  N7: LCD1.RS, Part1.A3
  N8: LCD1.DB2, Part1.A4/SDA
  N9: LCD1.DB4, Part1.A5/SCL

notes:
  As is connections. wag mo na pansinin number na nasa lcd.
  1-2-3-4-5-6-7
  ganyan numbering ng pins ng keypad pag nakaharap sayo pindutan
  ((walang keypad sa fritzing))
